# Fritzing sketch circuit (saved by Fritzing 0.9.2b)
perfboards: 1

parts:
  M3 = DC Motor
  M4 = DC Motor
  S1 = H-Bridge with L298N
  BAT1 = BC9VPC [package=bc9vpc]
  M5 = DC Motor
  M6 = DC Motor
  S2 = H-Bridge with L298N
  LED1 = LED - 5mm [color="Red (633nm)" package="5 mm [THT]"]
  LED2 = LED - 5mm [color="Red (633nm)" package="5 mm [THT]"]
  LED3 = LED - 5mm [color="Red (633nm)" package="5 mm [THT]"]
  LED4 = LED - 5mm [color="Red (633nm)" package="5 mm [THT]"]
  J1 = Piezo Speaker
  BAT2 = BC9VPC [package=bc9vpc]
  Eleman1 = Arduino Uno (Rev3)
  R1 = Resistor [tolerance=±5% resistance=220 package=THT]
  R2 = Resistor [tolerance=±5% resistance=220 package=THT]
  R3 = Resistor [tolerance=±5% resistance=220 package=THT]
  R4 = Resistor [tolerance=±5% resistance=220 package=THT]
  Eleman2 = Bluetooth Mate Silver

nets:
  N1: M3.pin_1, S1.M2-02
  N2: M3.pin_2, S1.M2-01, S2.ENA, S2.ENB, S2.ENA-5V, S2.ENB-5V, Eleman1.D11_PWM/MOSI
  N3: M4.pin_1, S2.M2-01
  N4: M4.pin_2, S2.M2-02
  N5: S1.12V, BAT1.V+
  N6: S1.ENA, S1.ENB, S1.ENA-5V, S1.ENB-5V
  N7: S1.M1-01, M5.pin_1
  N8: S1.M1-02, M5.pin_2
  N9: M6.pin_1, S2.M1-02
  N10: M6.pin_2, S2.M1-01
  N11: S2.12V, BAT2.V+
  N12: S2.IN1, Eleman1.D9_PWM
  N13: S2.IN2, Eleman1.D10_PWM/SS
  N14: S2.IN3, Eleman1.D13/SCK
  N15: S2.IN4, Eleman1.D12/MISO
  N16: LED1.anode, R1.Pin_0
  N17: LED2.anode, R3.Pin_0
  N18: LED3.anode, R4.Pin_0
  N19: LED4.anode, R2.Pin_0
  N20: J1.pin2, Eleman1.D6_PWM
  N21: Eleman1.D8, Eleman2.CTS_5V
  GND: Eleman1.GND, Eleman2.GND
  N22: Eleman1.D0/RX, Eleman2.TX_5V
  N23: Eleman1.D1/TX, Eleman2.RX_5V
  N24: Eleman1.D2, R3.Pin_1
  N25: Eleman1.D3_PWM, R4.Pin_1
  N26: Eleman1.D4, R2.Pin_1
  N27: Eleman1.D7, R1.Pin_1

custom parts:
  H-Bridge with L298N: h-bridge
